// Logisim project flipsnoflops.circ as structural Verilog
module flipflobrs (
  input  set,
  input  reset,
  output q,
  output nq
);

  nand nand_1 (q, ~set, nq);  // NAND_Gate
  nand nand_2 (nq, q, ~reset);  // NAND_Gate
endmodule

module flipflopRScoc (
  input  in_1,
  input  in_2,
  output out_3,
  output out_4
);

  wire clock_1_out, nand_1_out, nand_2_out;

  Clock clock_1 (.out(clock_1_out));
  nand nand_1 (nand_1_out, in_1, clock_1_out);
  nand nand_2 (nand_2_out, clock_1_out, in_2);
  flipflobrs flipflobrs_1 (.set(nand_1_out), .reset(nand_2_out), .q(out_3), .nq(out_4));
endmodule

module JK_GAL (
  input  preset,
  input  j,
  input  cock,
  input  k,
  input  clear,
  output q,
  output Nq
);

  wire nand_1_out, nand_2_out;

  nand nand_1 (nand_1_out, j, cock, Nq);
  nand nand_2 (nand_2_out, q, cock, k);
  nand nand_3 (q, preset, nand_1_out, Nq);
  nand nand_4 (Nq, q, nand_2_out, clear);
endmodule

module Jk_ME_PC (
  input  PS,
  input  j,
  input  clock,
  input  k,
  input  CLR,
  output q,
  output nq
);

  wire nand_1_out, nand_2_out, nand_3_out, nand_4_out, nand_5_out, nand_6_out, not_1_out, not_2_out,
       not_3_out;

  not not_1 (not_1_out, PS);
  nand nand_1 (nand_1_out, j, clock, nq);
  nand nand_2 (nand_2_out, q, clock, k);
  not not_2 (not_2_out, CLR);
  nand nand_3 (nand_3_out, not_1_out, nand_1_out, nand_4_out);
  nand nand_4 (nand_4_out, nand_3_out, nand_2_out, not_2_out);
  not not_3 (not_3_out, clock);
  nand nand_5 (nand_5_out, nand_3_out, not_3_out);
  nand nand_6 (nand_6_out, nand_4_out, not_3_out);
  nand nand_7 (q, not_1_out, nand_5_out, nq);
  nand nand_8 (nq, q, nand_6_out, not_2_out);
endmodule

module JK_ME_PC_T (
  input  PS,
  input  T,
  input  clock,
  input  CLR,
  output q,
  output nq
);

  wire nand_1_out, nand_2_out, nand_3_out, nand_4_out, nand_5_out, nand_6_out, not_1_out, not_2_out,
       not_3_out;

  not not_1 (not_1_out, PS);
  nand nand_1 (nand_1_out, T, clock, nq);
  nand nand_2 (nand_2_out, q, clock, T);
  not not_2 (not_2_out, CLR);
  nand nand_3 (nand_3_out, not_1_out, nand_1_out, nand_4_out);
  nand nand_4 (nand_4_out, nand_3_out, nand_2_out, not_2_out);
  not not_3 (not_3_out, clock);
  nand nand_5 (nand_5_out, nand_3_out, not_3_out);
  nand nand_6 (nand_6_out, nand_4_out, not_3_out);
  nand nand_7 (q, not_1_out, nand_5_out, nq);
  nand nand_8 (nq, q, nand_6_out, not_2_out);
endmodule

module JK_ME_PC_D (
  input  D,
  input  PS,
  input  clock,
  input  CLR,
  output q,
  output nq
);

  wire nand_1_out, nand_2_out, nand_3_out, nand_4_out, nand_5_out, nand_6_out, not_1_out, not_2_out,
       not_3_out, not_4_out;

  not not_1 (not_1_out, D);
  nand nand_1 (nand_1_out, D, clock, nq);
  nand nand_2 (nand_2_out, q, clock, not_1_out);
  not not_2 (not_2_out, PS);
  nand nand_3 (nand_3_out, not_2_out, nand_1_out, nand_4_out);
  nand nand_4 (nand_4_out, nand_3_out, nand_2_out, not_3_out);
  not not_3 (not_3_out, CLR);
  not not_4 (not_4_out, clock);
  nand nand_5 (nand_5_out, nand_3_out, not_4_out);
  nand nand_6 (nand_6_out, nand_4_out, not_4_out);
  nand nand_7 (q, not_2_out, nand_5_out, nq);
  nand nand_8 (nq, q, nand_6_out, not_3_out);
endmodule

module shifter_reg (
  input  preset,
  input  t,
  input  clock,
  input  clear,
  output out_5,
  output out_6,
  output out_7,
  output out_8
);

  // JK_ME_PC_T jk_me_pc_t_1: pin names not known
  Jk_ME_PC jk_me_pc_1 (.PS(preset), .j(t), .clock(clock), .k(t), .CLR(clear), .q(out_5));  // open: nq
  Jk_ME_PC jk_me_pc_2 (.PS(preset), .j(t), .clock(out_5), .k(t), .CLR(clear), .q(out_6));  // open: nq
  Jk_ME_PC jk_me_pc_3 (.PS(preset), .j(t), .clock(out_6), .k(t), .CLR(clear), .q(out_7));  // open: nq
  Jk_ME_PC jk_me_pc_4 (.PS(preset), .j(t), .clock(out_7), .k(t), .CLR(clear), .q(out_8));  // open: nq
  Hex_Digit_Display hex_digit_display_1 (.value({out_8, out_7, out_6, out_5}));  // open: dp
endmodule

module DIVfrenq (
  input  preset,
  input  t,
  input  clock,
  input  clear,
  output out_5,
  output out_6,
  output out_7,
  output out_8
);

  Jk_ME_PC jk_me_pc_1 (.PS(preset), .j(t), .clock(clock), .k(t), .CLR(clear), .q(out_5));  // open: nq
  Jk_ME_PC jk_me_pc_2 (.PS(preset), .j(t), .clock(out_5), .k(t), .CLR(clear), .q(out_6));  // open: nq
  Jk_ME_PC jk_me_pc_3 (.PS(preset), .j(t), .clock(out_6), .k(t), .CLR(clear), .q(out_7));  // open: nq
  Jk_ME_PC jk_me_pc_4 (.PS(preset), .j(t), .clock(out_7), .k(t), .CLR(clear), .q(out_8));  // open: nq
  Hex_Digit_Display hex_digit_display_1 (.value({out_8, out_7, out_6, out_5}));  // open: dp
endmodule
