// Logisim project demux.circ as structural Verilog
module demux2 (
  input  key,
  input  enable,
  output y1,
  output y2
);

  wire not_1_out;

  not not_1 (not_1_out, key);
  and and_1 (y1, not_1_out, enable);
  and and_2 (y2, key, enable);
endmodule

module dumux4 (
  input  enable,
  input  key0,
  input  key1,
  output y1,
  output y2,
  output y3,
  output y4
);

  wire demux2_1_y1, demux2_1_y2;

  demux2 demux2_1 (.key(key0), .enable(enable), .y1(demux2_1_y1), .y2(demux2_1_y2));
  demux2 demux2_2 (.key(key1), .enable(demux2_1_y1), .y1(y1), .y2(y2));
  demux2 demux2_3 (.key(key1), .enable(demux2_1_y2), .y1(y3), .y2(y4));
endmodule

module demux8 (
  input  enable,
  input  [2:0] key,
  output out_3,
  output out_4,
  output out_5,
  output out_6,
  output out_7,
  output out_8,
  output out_9,
  output out_10
);

  wire demux2_1_y1, demux2_1_y2;

  demux2 demux2_1 (.key(key[2]), .enable(enable), .y1(demux2_1_y1), .y2(demux2_1_y2));
  dumux4 dumux4_1 (.enable(demux2_1_y1), .key0(key[1]), .key1(key[0]), .y1(out_3), .y2(out_4), .y3(out_5), .y4(out_6));
  dumux4 dumux4_2 (.enable(demux2_1_y2), .key0(key[1]), .key1(key[0]), .y1(out_7), .y2(out_8), .y3(out_9), .y4(out_10));
endmodule

module bit4enable (
  input  [3:0] A,
  input  enable,
  output out_3,
  output out_4,
  output out_5,
  output out_6
);

  and and_1 (out_3, A[0], enable);
  and and_2 (out_4, A[1], enable);
  and and_3 (out_5, A[2], enable);
  and and_4 (out_6, A[3], enable);

  // Notes on the sheet:
  //   testar colocar isso antes de cada circuito como uma chave seletorra
endmodule
